# Fritzing sketch Board layout (saved by Fritzing 0.9.3b)
breadboards: 1

parts:
  Part2 = ESP32 Module Testbed  # not connected
  Part3 = ESP-WROOM-32 [ESP-32S] Module [part_number=ESP-WROOM-32]  # not connected
  DS1 = DS18B20 1-Wire Temperature Sensor [part_number=DS18B20]
  DS2 = DS18B20 1-Wire Temperature Sensor [part_number=DS18B20]
  DS3 = DS18B20 1-Wire Temperature Sensor [part_number=DS18B20]
  R1 = Resistor [tolerance=±5% resistance=220 package="0805 [SMD]"]
  R2 = Resistor [tolerance=±5% resistance=220 package="0805 [SMD]"]
  R3 = Resistor [tolerance=±5% resistance=220 package="0805 [SMD]"]
  R4 = Resistor [tolerance=±5% resistance=220 package="0805 [SMD]"]
  R5 = Resistor [tolerance=±5% resistance=220 package="0805 [SMD]"]
  LED5 = LED - 5mm [color="Blue (430nm)" package="5 mm [THT]"]
  LED6 = LED - 5mm [color="Red (633nm)" package="5 mm [THT]"]
  LED7 = LED - 5mm [color="Yellow (595nm)" package="5 mm [THT]"]
  LED8 = LED - 5mm [color="Green (555nm)" package="5 mm [THT]"]

nets:
  GND: DS1.GND, DS2.GND, DS3.GND, R2.Pin_0
  N1: DS1.DQ, DS2.DQ, DS3.DQ, R2.Pin_1
  VDD: DS1.VDD, DS2.VDD, DS3.VDD, R1.Pin_0, R3.Pin_0, R4.Pin_0, R5.Pin_0
  N2: R1.Pin_1, LED5.anode
  N3: R3.Pin_1, LED8.anode
  N4: R4.Pin_1, LED7.anode
  N5: R5.Pin_1, LED6.anode

custom parts:
  ESP32 Module Testbed: The ESP32 Module Testbed is a breadboard compatible breakout board for the ESP-WROOM-03 ESP32 module. The ESP32 is a WiFi and Bluetooth-enabled 32-bit, dual-core microcontroller.
  ESP-WROOM-32 [ESP-32S] Module: Espressif ESP-WROOM-32 WiFi/Bluetooth LE microcontroller module also known as the Ai-Thinker ESP-32S module with similar formfactor. The ESP32 is a microcontroller chip with WiFi and BLE capabilities. The chip is developed by Espressif and is the successor to the popular ESP8266 WiFi module.
