# Fritzing sketch Board layout (saved by Fritzing 0.9.3b)
breadboards: 1

parts:
  Part2 = ESP32 Module Testbed  # not connected
  Part3 = ESP-WROOM-32 [ESP-32S] Module [part_number=ESP-WROOM-32]  # not connected
  R2 = Resistor [tolerance=±5% resistance=220 package="0805 [SMD]"]
  DHT1 = DHT11 Humitidy and Temperature Sensor

nets:
  N1: R2.Pin_0, DHT1.VDD
  N2: R2.Pin_1, DHT1.DATA

custom parts:
  ESP32 Module Testbed: The ESP32 Module Testbed is a breadboard compatible breakout board for the ESP-WROOM-03 ESP32 module. The ESP32 is a WiFi and Bluetooth-enabled 32-bit, dual-core microcontroller.
  ESP-WROOM-32 [ESP-32S] Module: Espressif ESP-WROOM-32 WiFi/Bluetooth LE microcontroller module also known as the Ai-Thinker ESP-32S module with similar formfactor. The ESP32 is a microcontroller chip with WiFi and BLE capabilities. The chip is developed by Espressif and is the successor to the popular ESP8266 WiFi module.
  DHT11 Humitidy and Temperature Sensor: DHT11 Humidity and Temperature Sensor
